# Fritzing sketch Ard mini Maket (saved by Fritzing 0.9.9b)
perfboards: 2

parts:
  Arduino1 = Arduino Mini (Rev5)
  J1 = shrouded pin header, 26 pins [form="♂ (shrouded male)"]
  J2 = male pin header, 5 pins [form="♂ (male)"]
  S1 = SWITCH-DPDT [package=ayz0202]
  C1 = Ceramic Capacitor [capacitance=0.22µF voltage=35V package="100 mil [THT, multilayer]"]
  Q1 = NPN-Transistor [package="TO92 [THT]"]
  R1 = Resistor [tolerance=±5% resistance=2.2k package=THT]
  C2 = Ceramic Capacitor [capacitance=100nF voltage=35V package="100 mil [THT, multilayer]"]
  J3 = male pin header, 2 pins [form="♂ (male)"]

nets:
  N1: Arduino1.D0/TX, S1.5
  N2: Arduino1.D1/RX, S1.2
  N3: Arduino1.RESET, C1.1
  N4: Arduino1.GND, J1.pin3, J1.pin7, J1.pin19, J1.pin23, J2.pin4, Q1.E, C2.0
  N5: Arduino1.D2, J1.pin16
  N6: Arduino1.D3_PWM, J1.pin15
  N7: Arduino1.D4, J1.pin14
  N8: Arduino1.D5_PWM, J1.pin2
  N9: Arduino1.D6_PWM, J1.pin1
  N10: Arduino1.D7, J1.pin18
  N11: Arduino1.D8, J1.pin17
  N12: Arduino1.D9_PWM, J1.pin13
  N13: Arduino1.VCC, J1.pin22
  N14: Arduino1.5V, J1.pin5, J1.pin6, J2.pin5
  N15: Arduino1.A3, J1.pin11
  N16: Arduino1.A2, J1.pin10
  N17: Arduino1.A1, Q1.C
  N18: Arduino1.A0, J1.pin9
  N19: Arduino1.D13, J1.pin8
  N20: Arduino1.D12, J1.pin12
  N21: Arduino1.D11_PWM, J1.pin21
  N22: Arduino1.D10_PWM, J1.pin20
  N23: Arduino1.A6, J1.pin4
  N24: Arduino1.A4, J3.pin1
  N25: Arduino1.A5, J3.pin2
  N26: J1.pin24, R1.Pin_0
  N27: J1.pin25, S1.6
  N28: J1.pin26, S1.1
  N29: J2.pin1, C1.0
  N30: J2.pin2, S1.3
  N31: J2.pin3, S1.4
  N32: Q1.B, R1.Pin_1, C2.1
