# Fritzing sketch keypad_w_leds (saved by Fritzing 0.9.9b)
breadboards: 1

parts:
  S1 = SWITCH-MOMENTARY-2 [package=tactile-pth]
  S2 = SWITCH-MOMENTARY-2 [package=tactile-pth]
  S3 = SWITCH-MOMENTARY-2 [package=tactile-pth]
  S4 = SWITCH-MOMENTARY-2 [package=tactile-pth]
  S5 = SWITCH-MOMENTARY-2 [package=tactile-pth]
  S6 = SWITCH-MOMENTARY-2 [package=tactile-pth]
  S7 = SWITCH-MOMENTARY-2 [package=tactile-pth]
  S8 = SWITCH-MOMENTARY-2 [package=tactile-pth]
  S9 = SWITCH-MOMENTARY-2 [package=tactile-pth]
  S10 = SWITCH-MOMENTARY-2 [package=tactile-pth]
  S11 = SWITCH-MOMENTARY-2 [package=tactile-pth]
  S12 = SWITCH-MOMENTARY-2 [package=tactile-pth]
  PIN2 = LEDs [package=led10mm]
  PIN4 = LEDs [package=led10mm]
  PIN6 = LEDs [package=led10mm]
  PIN7 = LEDs [package=led10mm]
  PIN1 = LEDs [package=led10mm]
  PIN3 = LEDs [package=led10mm]
  PIN5 = LEDs [package=led10mm]

nets:
  N1: S1.1, S2.1, S3.1, PIN2.A
  N2: S1.2, S4.2, S7.2, S10.2, PIN1.C
  N3: S2.2, S5.2, S8.2, S11.2, PIN3.C
  N4: S3.2, S6.2, S9.2, S12.2, PIN5.C
  N5: S4.1, S5.1, S6.1, PIN4.A
  N6: S7.1, S8.1, S9.1, PIN6.A
  N7: S10.1, S11.1, S12.1, PIN7.A
