# Fritzing sketch newSerialLock (saved by Fritzing 0.9.9b)
breadboards: 1

parts:
  Arduino_Mini = Arduino Pro Mini v13
  Arduino_Mega_2560 = Arduino Mega 2560 (Rev3)
  Q2 = Basic FET N-Channel [package="DPak [SMD]"]
  Q1 = Basic FET N-Channel [package="DPak [SMD]"]
  R1 = Resistor [tolerance=±5% resistance=4.7k package=THT]
  R2 = Resistor [tolerance=±5% resistance=4.7k package=THT]

nets:
  N1: Arduino_Mini.D0/TX, Q1.drain
  N2: Arduino_Mini.D1/RX, Q2.source, R2.Pin_0
  N3: Arduino_Mini.VCC, Q2.Gate, R2.Pin_1
  GND: Arduino_Mini.GND, Arduino_Mega_2560.GND
  N4: Arduino_Mega_2560.D19/RX1, Q1.source, R1.Pin_0
  N5: Arduino_Mega_2560.D18/TX1, Q2.drain
  N6: Arduino_Mega_2560.5V, Q1.Gate, R1.Pin_1
