# Fritzing sketch wholeProject (saved by Fritzing 0.9.9b)

parts:
  Q1 = NPN-Transistor [package="TO92 [THT]"]
  Q2 = NPN-Transistor [package="TO92 [THT]"]
  Q3 = TRANSISTOR_NPN [package=to-92]
  R1 = Resistor [tolerance=±5% resistance=1k package="0805 [SMD]"]
  R2 = Resistor [tolerance=±5% resistance=10k package="0805 [SMD]"]
  MAIN_CONTROLLER = Arduino Mega 2560 (Rev3)
  R3 = Resistor [tolerance=±5% resistance=100k package=THT]
  R4 = Resistor [tolerance=±5% resistance=10k package="0805 [SMD]"]
  SECOND_CONTROLLER = Arduino Pro Mini v13
  Power2 = Power plug
  R5 = Resistor [tolerance=±5% resistance=15k package=THT]
  D1 = Rectifier Diode [part_number=1N4001 package="300 mil [THT]"]
  R6 = Resistor [tolerance=±5% resistance=200 package=THT]
  D2 = Rectifier Diode [part_number=1N4001 package="300 mil [THT]"]
  R7 = Resistor [tolerance=±5% resistance=430 package=THT]
  Q4 = Basic FET P-Channel [package="DPak [SMD]"]
  C1 = Ceramic Capacitor [capacitance=2.2nF voltage=35V package="100 mil [THT, multilayer]"]
  Q5 = Basic FET P-Channel [package="DPak [SMD]"]
  L1 = Inductor [inductance=220mH package="400 mil [THT]"]
  C2 = Electrolytic Capacitor [capacitance=470µF voltage=35V package="100 mil [THT, electrolytic]"]
  D3 = Rectifier Diode [part_number=1N4001 package="300 mil [THT]"]
  U1 = Voltage Regulator [package=to220-adj]
  Power1 = Power plug
  DS2Y-5-DC5V1 = DS2Y-5-DC5V [part_number=DS2Y-5-DC5V]
  S1 = SPST Switch [package=switch-spdt_kit]
  D4 = Schottky Diode [part_number=1N5817 package="Melf DO-213 AB [SMD]"]
  D5 = Rectifier Diode [part_number=1N4001 package="300 mil [THT]"]
  D6 = Rectifier Diode [part_number=1N4001 package="300 mil [THT]"]
  R8 = Resistor [tolerance=±5% resistance=220 package=THT]
  Q6 = NPN-Transistor [package="TO92 [THT]"]
  R9 = Resistor [tolerance=±5% resistance=220 package=THT]
  R10 = Resistor [tolerance=±5% resistance=1k package=THT]
  R11 = TRIMPOT [package=3362u-2]
  R12 = Resistor [tolerance=±5% resistance=470 package=THT]
  R13 = Resistor [tolerance=±5% resistance=220 package=THT]
  C3 = Ceramic Capacitor [capacitance=100nF voltage=35V package="100 mil [THT, multilayer]"]
  C4 = Electrolytic Capacitor [capacitance=47µF voltage=35V package="100 mil [THT, electrolytic]"]
  C5 = Ceramic Capacitor [capacitance=300nF voltage=35V package="100 mil [THT, multilayer]"]
  DS2Y-5-DC5V2 = DS2Y-5-DC5V [part_number=DS2Y-5-DC5V]
  D7 = Schottky Diode [part_number=1N5817 package="Melf DO-213 AB [SMD]"]
  Q7 = NPN-Transistor [package="SOT-23 [SMD]"]
  R14 = Resistor [tolerance=±5% resistance=1k package=THT]
  Q8 = NPN-Transistor [package="TO92 [THT]"]
  Q9 = NPN-Transistor [package="TO92 [THT]"]
  R15 = Resistor [tolerance=±5% resistance=220 package=THT]
  R16 = Resistor [tolerance=±5% resistance=220 package=THT]
  R17 = Resistor [tolerance=±5% resistance=500 package=THT]
  R18 = Resistor [tolerance=±5% resistance=500 package=THT]
  R19 = Resistor [tolerance=±5% resistance=100 package="0805 [SMD]"]
  LED1 = LEDs [package=led-0603]
  R20 = Resistor [tolerance=±5% resistance=100 package="0805 [SMD]"]
  LED2 = LEDs [package=led-0603]
  R21 = Resistor [tolerance=±5% resistance=100 package="0805 [SMD]"]
  LED3 = LEDs [package=led-0603]
  R22 = Resistor [tolerance=±5% resistance=100 package="0805 [SMD]"]
  LED4 = LEDs [package=led-0603]
  C6 = Ceramic Capacitor [capacitance=100nF voltage=35V package="100 mil [THT, multilayer]"]
  C7 = Ceramic Capacitor [capacitance=15pF voltage=35V package="100 mil [THT, multilayer]"]
  R23 = Resistor [tolerance=±5% resistance=100 package="0805 [SMD]"]
  R24 = Resistor [tolerance=±5% resistance=100 package="0805 [SMD]"]
  R25 = Resistor [tolerance=±5% resistance=100 package="0805 [SMD]"]
  R26 = Resistor [tolerance=±5% resistance=100 package="0805 [SMD]"]
  LED5 = LEDs [package=led-0603]
  LED6 = LEDs [package=led-0603]
  LED7 = LEDs [package=led-0603]
  LED8 = LEDs [package=led-0603]
  C8 = Ceramic Capacitor [capacitance=15pF voltage=35V package="100 mil [THT, multilayer]"]
  C9 = Ceramic Capacitor [capacitance=100nF voltage=35V package="100 mil [THT, multilayer]"]
  F1 = Fan - Ventilador [package=THT]
  Q10 = NPN-Transistor [package="TO92 [THT]"]
  R27 = Resistor [tolerance=±5% resistance=220 package=THT]
  C10 = Electrolytic Capacitor [capacitance=22µF voltage=35V package="100 mil [THT, electrolytic]"]
  C11 = Ceramic Capacitor [capacitance=100nF voltage=35V package="100 mil [THT, multilayer]"]
  LED9 = LEDs [package=led10mm]
  R28 = Resistor [tolerance=±5% resistance=1k package=THT]
  IC1 = Voltage Regulator [package=to-220-alt]
  C12 = Ceramic Capacitor [capacitance=300nF voltage=35V package="100 mil [THT, multilayer]"]
  C13 = Ceramic Capacitor [capacitance=100nF voltage=35V package="100 mil [THT, multilayer]"]
  NEXTION_DISPLAY = Nextion SPI 2.4" LCD NX3224T024_011
  C14 = Electrolytic Capacitor [capacitance=22µF voltage=35V package="100 mil [THT, electrolytic]"]
  R29 = Resistor [tolerance=±5% resistance=50 package=THT]
  R30 = Resistor [tolerance=±5% resistance=50 package=THT]

nets:
  N1: Q1.E, Q2.C
  N2: Q1.B, R4.Pin_1
  N3: Q1.C, MAIN_CONTROLLER.5V, R4.Pin_0, D1.anode
  N4: Q2.E, R1.Pin_0, R2.Pin_0, C1.1
  N5: Q2.B, R5.Pin_1
  GND: Q3.E, R1.Pin_1, MAIN_CONTROLLER.GND, SECOND_CONTROLLER.GND, Power2.GND, C1.0, C2.-, D3.anode, Power1.GND, DS2Y-5-DC5V1.1_+, S1.O, D4.anode, Q6.E, R12.Pin_1, C3.0, C4.-, C5.0, Q7.2, R17.Pin_1, R18.Pin_1, Q10.E, C10.-, C11.0, R28.Pin_1, IC1.GND, C12.1, C13.1, NEXTION_DISPLAY.GND, C14.-, R29.Pin_1, R30.Pin_1
  N6: Q3.B, R2.Pin_1
  N7: Q3.C, R3.Pin_1, Q4.Gate, Q5.Gate
  N8: MAIN_CONTROLLER.A0, DS2Y-5-DC5V1.8_N.O.
  N9: MAIN_CONTROLLER.D17_PWM/RX2, Q4.drain
  N10: MAIN_CONTROLLER.D16_PWM/TX2, Q5.source
  N11: MAIN_CONTROLLER.D15/RX3, NEXTION_DISPLAY.pin2
  N12: MAIN_CONTROLLER.D14/TX3, NEXTION_DISPLAY.pin3
  N13: MAIN_CONTROLLER.D13_PWM, LED9.A
  N14: MAIN_CONTROLLER.D12_PWM, R27.Pin_0
  N15: MAIN_CONTROLLER.VIN, DS2Y-5-DC5V1.9_N.O., R10.Pin_1, R11.WIPER, R11.CW, IC1.IN, C12.0
  N16: MAIN_CONTROLLER.D52, R14.Pin_0
  N17: MAIN_CONTROLLER.D53, R9.Pin_0
  N18: R3.Pin_0, R6.Pin_1, R7.Pin_1
  N19: SECOND_CONTROLLER.RAW, U1.OUT, R13.Pin_1, C3.1, C4.+, DS2Y-5-DC5V2.4_COM
  N20: SECOND_CONTROLLER.D11_PWM/MOSI, R15.Pin_0
  N21: SECOND_CONTROLLER.D10_PWM/SS, R16.Pin_0
  N22: SECOND_CONTROLLER.D1/RX, Q5.drain
  N23: SECOND_CONTROLLER.D0/TX, Q4.source
  N24: Power2.VCC, L1.pin_1, D3.cathode
  N25: R5.Pin_0, D2.anode, L1.pin_0, C2.+, U1.IN, C5.1, DS2Y-5-DC5V2.16_-, DS2Y-5-DC5V2.13_COM, D7.cathode, Q8.C, Q9.C
  N26: D1.cathode, R6.Pin_0
  N27: D2.cathode, R7.Pin_0
  N28: U1.ADJ, R12.Pin_0, R13.Pin_0
  N29: Power1.VCC, DS2Y-5-DC5V1.13_COM, S1.S
  N30: DS2Y-5-DC5V1.4_COM, S1.P, R8.Pin_0
  N31: DS2Y-5-DC5V1.16_-, D4.cathode, D5.cathode, D6.cathode, Q6.C
  N32: D5.anode, R10.Pin_0, R11.CCW
  N33: D6.anode, R8.Pin_1
  N34: Q6.B, R9.Pin_1
  N35: DS2Y-5-DC5V2.8_N.O., F1.5V, C10.+, C11.1
  N36: DS2Y-5-DC5V2.1_+, D7.anode, Q7.1
  N37: Q7.0, R14.Pin_1
  N38: Q8.E, R17.Pin_0, C6.0, C7.0
  N39: Q8.B, R15.Pin_1
  N40: Q9.E, R18.Pin_0, R23.Pin_0, R24.Pin_0, R25.Pin_0, R26.Pin_0, C8.0, C9.0
  N41: Q9.B, R16.Pin_1
  N42: R19.Pin_0, R20.Pin_0, R21.Pin_0, R22.Pin_0
  N43: R19.Pin_1, LED1.A
  N44: LED1.C, LED2.C, LED3.C, LED4.C, C6.1, C7.1, R29.Pin_0
  N45: R20.Pin_1, LED2.A
  N46: R21.Pin_1, LED3.A
  N47: R22.Pin_1, LED4.A
  N48: R23.Pin_1, LED8.A
  N49: R24.Pin_1, LED7.A
  N50: R25.Pin_1, LED5.A
  N51: R26.Pin_1, LED6.A
  N52: LED5.C, LED6.C, LED7.C, LED8.C, C8.1, C9.1, R30.Pin_0
  N53: F1.GND, Q10.C
  N54: Q10.B, R27.Pin_1
  N55: LED9.C, R28.Pin_0
  N56: IC1.OUT, C13.0, NEXTION_DISPLAY.VCC, C14.+

custom parts:
  Fan - Ventilador: Ventilador de 2 pines, se encuentra comunmente en computadoras de escritorio
